# Fritzing sketch PyroCircuit (saved by Fritzing 0.9.3b)
circuit board: 3.90076cm x 2.44746cm
breadboards: 2

parts:
  LED3 = LED - 3mm [color="Red (633nm)" package="3 mm [THT]"]
  R5 = Resistor [tolerance=±5% resistance=10k package=THT]
  R6 = Resistor [tolerance=±5% resistance=470 package=THT]
  FET2 = STP16NF06 N-Channel Power MOSFET
  JP2 = Header 4 [package=molex-1x4_lock]
  J3 = Screw terminal - 2 pins [package=THT]
  FET3 = STP16NF06 N-Channel Power MOSFET
  LED4 = LED - 3mm [color="Red (633nm)" package="3 mm [THT]"]
  R7 = Resistor [tolerance=±5% resistance=10k package=THT]
  R8 = Resistor [tolerance=±5% resistance=470 package=THT]
  J4 = Screw terminal - 2 pins [package=THT]

nets:
  N1: LED3.cathode, R5.Pin_1, FET2.source, JP2.2, FET3.source, LED4.cathode, R7.Pin_1
  N2: LED3.anode, R6.Pin_1
  N3: R5.Pin_0, FET2.gate, JP2.1
  N4: R6.Pin_0, FET2.drain, J3.pin1
  N5: JP2.3, J3.pin2, J4.pin2
  N6: JP2.4, FET3.gate, LED4.anode, R7.Pin_0, R8.Pin_1
  N7: FET3.drain, R8.Pin_0, J4.pin1

custom parts:
  STP16NF06 N-Channel Power MOSFET: STP16NF06 N-channel Power MOSFET
