# Fritzing sketch altimeter_baro_only (saved by Fritzing 0.9.3b)
circuit board: 7.38355cm x 2.66481cm
breadboards: 1

parts:
  3v_Pro_Tricket = Pro Trinket 3.3V
  BMP280 = BMP280 Breakout
  microSD = MicroSD Breakout

nets:
  GND: 3v_Pro_Tricket.GND, BMP280.GND, microSD.GND
  3.3V: 3v_Pro_Tricket.+3V3, BMP280.VIN, microSD.5V
  N1: 3v_Pro_Tricket.D4, microSD.CS
  N2: 3v_Pro_Tricket.D3, BMP280.CS
  N3: 3v_Pro_Tricket.D11, BMP280.SDI, microSD.DI
  N4: 3v_Pro_Tricket.D12, BMP280.SDO, microSD.DO
  N5: 3v_Pro_Tricket.D13, BMP280.SCK, microSD.CLK

custom parts:
  Pro Trinket 3.3V: The Pro Trinket 3.3V is like an Arduino Pro Mini with more pins and USB included. However, it uses 3V logic and 12MHz clock which means it's good when you want a lower-power and lower-voltage setup. Built with the common core Arduino chip, the ATmega328p, it has 18 GPIO, 2 extra analog inputs, 28K of flash, and 2K of RAM. It has onboard USB bootloading support with Optiboot support, so you can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
  BMP280 Breakout: A breakout for the BMP280 barometric pressure and temperature sensor
  MicroSD Breakout: 5V-ready microSD Breakout with Level Shifter
