# Fritzing sketch arduino_schematic (saved by Fritzing 0.9.3b)
circuit board: 14.4661cm x 2.56114cm
breadboards: 2

parts:
  FET2 = STP16NF06 N-Channel Power MOSFET
  R1 = Resistor [tolerance=±5% resistance=10k package=THT]
  R2 = Resistor [tolerance=±5% resistance=10k package=THT]
  R3 = Resistor [tolerance=±5% resistance=470 package=THT]
  3v_Pro_Tricket = Pro Trinket 3.3V
  R4 = Resistor [tolerance=±5% resistance=470 package=THT]
  J3 = screw terminal, 2 pins
  J2 = screw terminal, 2 pins
  J5 = screw terminal, 2 pins
  J4 = screw terminal, 2 pins
  SG1 = Buzzer 12mm [package=buzzer-12mm-ns-kit]
  FET1 = STP16NF06 N-Channel Power MOSFET
  LED2 = LED - 3mm [color="Red (633nm)" package="3 mm [THT]"]
  LED1 = LED - 3mm [color="Red (633nm)" package="3 mm [THT]"]
  BMP280 = BMP280 Breakout
  LIS3DH = LIS3DH Accelerometer Breakout
  microSD = MicroSD Breakout
  C1 = Capacitor Polarized [package=cpol-radial-10uf-25v]
  C2 = Tantalum Capacitor [capacitance=100nF voltage=50V package="200 mil [THT, tantalum]"]
  U1 = Voltage Regulator [package=to220-igo]

nets:
  N1: FET2.gate, R1.Pin_0, 3v_Pro_Tricket.A5
  N2: FET2.drain, R3.Pin_1, J3.pin2
  GND: FET2.source, R1.Pin_1, R2.Pin_1, 3v_Pro_Tricket.GND, J4.pin2, SG1.2, FET1.source, LED2.cathode, LED1.cathode, BMP280.GND, LIS3DH.GND, microSD.GND, C1.-, C2.-, U1.GND
  N3: R2.Pin_0, 3v_Pro_Tricket.D6, FET1.gate
  N4: R3.Pin_0, LED1.anode
  N5: 3v_Pro_Tricket.VBAT, J3.pin1, J2.pin2, C1.+, U1.IN
  3.3V: 3v_Pro_Tricket.+3V3, BMP280.VIN, LIS3DH.Vin, microSD.5V
  N6: 3v_Pro_Tricket.D8, SG1.1
  N7: 3v_Pro_Tricket.D5, LIS3DH.Test
  N8: 3v_Pro_Tricket.D4, microSD.CS
  N9: 3v_Pro_Tricket.D3, BMP280.CS
  N10: 3v_Pro_Tricket.D11, BMP280.SDI, LIS3DH.Yout, microSD.DI
  N11: 3v_Pro_Tricket.D12, BMP280.SDO, LIS3DH.Zout, microSD.DO
  N12: 3v_Pro_Tricket.D13, BMP280.SCK, LIS3DH.Xout, microSD.CLK
  N13: R4.Pin_0, LED2.anode
  N14: R4.Pin_1, J2.pin1, FET1.drain
  N15: J5.pin1, C2.+, U1.OUT
  N16: J5.pin2, J4.pin1

notes:
  M
  D
  -
  +
  SW

custom parts:
  STP16NF06 N-Channel Power MOSFET: STP16NF06 N-channel Power MOSFET
  Pro Trinket 3.3V: The Pro Trinket 3.3V is like an Arduino Pro Mini with more pins and USB included. However, it uses 3V logic and 12MHz clock which means it's good when you want a lower-power and lower-voltage setup. Built with the common core Arduino chip, the ATmega328p, it has 18 GPIO, 2 extra analog inputs, 28K of flash, and 2K of RAM. It has onboard USB bootloading support with Optiboot support, so you can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
  BMP280 Breakout: A breakout for the BMP280 barometric pressure and temperature sensor
  LIS3DH Accelerometer Breakout: LIS3DH Accelerometer Breakout board
  MicroSD Breakout: 5V-ready microSD Breakout with Level Shifter
