# Fritzing sketch arduino_schematic_with_ADXL377 (saved by Fritzing 0.9.3b)
circuit board: 10.5975cm x 4.54354cm
breadboards: 2

parts:
  FET2 = STP16NF06 N-Channel Power MOSFET
  R1 = Resistor [tolerance=±5% resistance=10k package=THT]
  R2 = Resistor [tolerance=±5% resistance=10k package=THT]
  R4 = Resistor [tolerance=±5% resistance=470 package=THT]
  J3 = screw terminal, 2 pins
  J2 = screw terminal, 2 pins
  J5 = screw terminal, 2 pins
  J4 = screw terminal, 2 pins
  FET1 = STP16NF06 N-Channel Power MOSFET
  LED2 = LED - 3mm [color="Red (633nm)" package="3 mm [THT]"]
  LED1 = LED - 3mm [color="Red (633nm)" package="3 mm [THT]"]
  BMP280 = BMP280 Breakout
  C1 = Capacitor Polarized [package=cpol-radial-10uf-25v]
  C2 = Tantalum Capacitor [capacitance=100nF voltage=50V package="200 mil [THT, tantalum]"]
  U1 = Voltage Regulator [package=to220-igo]
  Part1 = Adafruit ADXL377 [part_number="Adafruit #1413"]
  Part2 = Adafruit Feather M0 Adalogger [part_number="Adafruit #2796"]
  LIS3DH = LIS3DH Accelerometer Breakout
  R3 = Resistor [tolerance=±5% resistance=470 package=THT]

nets:
  N1: FET2.gate, R1.Pin_0
  N2: FET2.drain, J3.pin2, R3.Pin_1
  GND: FET2.source, R1.Pin_1, R2.Pin_1, J4.pin2, FET1.source, LED2.cathode, LED1.cathode, BMP280.GND, C1.-, C2.-, U1.GND, Part1.GND, Part2.GND, LIS3DH.GND
  N3: R2.Pin_0, FET1.gate
  N4: R4.Pin_0, LED2.anode
  N5: R4.Pin_1, J2.pin1, FET1.drain
  3.3V: J3.pin1, J2.pin2, BMP280.VIN, C1.+, U1.IN, Part1.VIN, Part2.+3V3, LIS3DH.Vin
  N6: J5.pin1, C2.+, U1.OUT
  N7: J5.pin2, J4.pin1
  N8: LED1.anode, R3.Pin_0
  N9: BMP280.SCK, Part2.SCK, LIS3DH.Xout
  N10: BMP280.SDO, Part2.MISO, LIS3DH.Zout
  N11: BMP280.SDI, Part2.MOSI, LIS3DH.Yout
  N12: BMP280.CS, Part2.D0
  N13: Part1.ZOUT, Part2.A0
  N14: Part1.YOUT, Part2.A1
  N15: Part1.XOUT, Part2.A2
  N16: Part2.D1, LIS3DH.Test

notes:
  M
  D
  -
  +
  SW

custom parts:
  STP16NF06 N-Channel Power MOSFET: STP16NF06 N-channel Power MOSFET
  BMP280 Breakout: A breakout for the BMP280 barometric pressure and temperature sensor
  Adafruit ADXL377: Hey rocket man (burnin' out your fuse out there alone) ever wonder how fast you're rocketing? The ADXL377 +-200g 3-axis accelerometer may be able to tell the answer. You read that right, this accelerometer can sense up to 200g's of force. Incredible! Not surprisingly, we couldn't say "no" to a breakout for this sensor. The sensor is soldered onto a PCB with four mounting holes (in case you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
  Adafruit Feather M0 Adalogger: This is the Adafruit Feather M0 Adalogger - our take on an 'all-in-one' Cortex M0 datalogger (or data-reader) with built in USB and battery charging. Its an Adafruit Feather M0 with a microSD holder ready to rock! We have other boards in the Feather family, check'em out here At the Feather M0's heart is an ATSAMD21G18 ARM Cortex M0 processor, clocked at 48 MHz and at 3.3V logic, the same one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
  LIS3DH Accelerometer Breakout: LIS3DH Accelerometer Breakout board
