# Fritzing sketch arduino_schematic_with_ADXL377_without_pyro (saved by Fritzing 0.9.3b)
circuit board: 6.36085cm x 4.69668cm
breadboards: 1

parts:
  BMP280 = BMP280 Breakout
  Part1 = Adafruit ADXL377 [part_number="Adafruit #1413"]
  Part2 = Adafruit Feather M0 Adalogger [part_number="Adafruit #2796"]
  LIS3DH = LIS3DH Accelerometer Breakout

nets:
  3.3V: BMP280.VIN, Part1.VIN, Part2.+3V3, LIS3DH.Vin
  GND: BMP280.GND, Part1.GND, Part2.GND, LIS3DH.GND
  N1: BMP280.SCK, Part2.SCK, LIS3DH.Xout
  N2: BMP280.SDO, Part2.MISO, LIS3DH.Zout
  N3: BMP280.SDI, Part2.MOSI, LIS3DH.Yout
  N4: BMP280.CS, Part2.D0
  N5: Part1.ZOUT, Part2.A0
  N6: Part1.YOUT, Part2.A1
  N7: Part1.XOUT, Part2.A2
  N8: Part2.D1, LIS3DH.Test

custom parts:
  BMP280 Breakout: A breakout for the BMP280 barometric pressure and temperature sensor
  Adafruit ADXL377: Hey rocket man (burnin' out your fuse out there alone) ever wonder how fast you're rocketing? The ADXL377 +-200g 3-axis accelerometer may be able to tell the answer. You read that right, this accelerometer can sense up to 200g's of force. Incredible! Not surprisingly, we couldn't say "no" to a breakout for this sensor. The sensor is soldered onto a PCB with four mounting holes (in case you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
  Adafruit Feather M0 Adalogger: This is the Adafruit Feather M0 Adalogger - our take on an 'all-in-one' Cortex M0 datalogger (or data-reader) with built in USB and battery charging. Its an Adafruit Feather M0 with a microSD holder ready to rock! We have other boards in the Feather family, check'em out here At the Feather M0's heart is an ATSAMD21G18 ARM Cortex M0 processor, clocked at 48 MHz and at 3.3V logic, the same one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
  LIS3DH Accelerometer Breakout: LIS3DH Accelerometer Breakout board
