# Fritzing sketch arduino_schematic (saved by Fritzing 0.9.0b)
circuit board: 16.3cm x 2.75cm
breadboards: 2

parts:
  FET2 = STP16NF06 N-Channel Power MOSFET
  FET3 = STP16NF06 N-Channel Power MOSFET
  R1 = Resistor [tolerance=±5% resistance=10k package=THT]
  R2 = Resistor [tolerance=±5% resistance=10k package=THT]
  R3 = Resistor [tolerance=±5% resistance=470 package=THT]
  3v_Pro_Tricket = Pro Trinket 3.3V
  R4 = Resistor [tolerance=±5% resistance=470 package=THT]
  J3 = screw terminal, 2 pins
  J2 = screw terminal, 2 pins
  J5 = screw terminal, 2 pins
  J4 = screw terminal, 2 pins
  SG1 = Buzzer 12mm [package=buzzer-12mm-ns-kit]
  FET1 = STP16NF06 N-Channel Power MOSFET
  LED2 = LED - 3mm [color="Red (633nm)" package="3 mm [THT]"]
  LED1 = LED - 3mm [color="Red (633nm)" package="3 mm [THT]"]
  BMP280 = BMP280 Breakout
  LIS3DH = LIS3DH Accelerometer Breakout
  microSD = MicroSD Breakout
  part = STP16NF06 N-Channel Power MOSFET  # not connected

nets:
  N1: FET2.gate, R1.Pin_0, 3v_Pro_Tricket.D4
  N2: FET2.drain, R3.Pin_1, J3.pin1
  GND: FET2.source, FET3.source, R1.Pin_1, R2.Pin_1, 3v_Pro_Tricket.GND, SG1.2, FET1.source, LED2.cathode, LED1.cathode, BMP280.GND, LIS3DH.GND, microSD.GND
  12V: FET3.gate, 3v_Pro_Tricket.VBAT, J3.pin2, J2.pin2, J4.pin1
  N3: FET3.drain, J5.pin2
  N4: R2.Pin_0, 3v_Pro_Tricket.D3, FET1.gate
  N5: R3.Pin_0, LED1.anode
  3.3V: 3v_Pro_Tricket.+3V3, BMP280.VIN, LIS3DH.Vin, microSD.5V
  N6: 3v_Pro_Tricket.D6, SG1.1
  N7: 3v_Pro_Tricket.D5, LIS3DH.Test
  N8: 3v_Pro_Tricket.D9, microSD.CS
  N9: 3v_Pro_Tricket.D10, BMP280.CS
  N10: 3v_Pro_Tricket.D11, BMP280.SDI, LIS3DH.Yout, microSD.DI
  N11: 3v_Pro_Tricket.D12, BMP280.SDO, LIS3DH.Zout, microSD.DO
  N12: 3v_Pro_Tricket.D13, LIS3DH.Xout, microSD.CLK
  N13: R4.Pin_0, LED2.anode
  N14: R4.Pin_1, J2.pin1, FET1.drain
  N15: J5.pin1, J4.pin2

notes:
  +
  -
  SW
  MAIN
  DROGUE

custom parts:
  STP16NF06 N-Channel Power MOSFET: STP16NF06 N-channel Power MOSFET
  Pro Trinket 3.3V: The Pro Trinket 3.3V is like an Arduino Pro Mini with more pins and USB included. However, it uses 3V logic and 12MHz clock which means it's good when you want a lower-power and lower-voltage setup. Built with the common core Arduino chip, the ATmega328p, it has 18 GPIO, 2 extra analog inputs, 28K of flash, and 2K of RAM. It has onboard USB bootloading support with Optiboot support, so you can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
  BMP280 Breakout: A breakout for the BMP280 barometric pressure and temperature sensor
  LIS3DH Accelerometer Breakout: LIS3DH Accelerometer Breakout board
  MicroSD Breakout: 5V-ready microSD Breakout with Level Shifter
